// Logisim project cpu.circ as structural Verilog: 1 circuit, main circuit cpu
// MemData
module cpu (
  input  clk,
  input  [31:0] Instruction,
  input  [31:0] MemReadData,
  output [31:0] MemAddress,
  output [31:0] ProgramCounter,
  output [31:0] ra,
  output [31:0] sp,
  output [31:0] t0,
  output [31:0] t1,
  output [31:0] t2,
  output [31:0] s0,
  output [31:0] s1,
  output [31:0] a0,
  output [3:0] MemWriteMask,
  output [31:0] MemWriteData
);

  wire ASel, BrEq, BrLt, BrUn, BSel, MemRW, PCSel, RegWEn;
  wire [1:0] WBSel;
  wire [2:0] ImmSel;
  wire [3:0] ALUSel;
  wire [11:0] Immd;
  wire [19:0] NextInstruction;
  wire [31:0] ALUInputA, ALUInputB, DataToReg, Immediate, IncreasedPC, NextIncreasedPC, NextPC,
       NowIncreasedPC, NowInstruction, ReadData1, ReadData2, WriteBack;

  Adder #(.width(32)) adder_1 (.a(ProgramCounter), .b(32'h4), .out(IncreasedPC));  // open: cin, cout
  Register #(.width(32)) PC (.D(NowIncreasedPC), .clk(clk), .Q(ProgramCounter));  // open: en, clr
  Multiplexer #(.width(32)) multiplexer_1 (.in0(IncreasedPC), .in1(MemAddress), .out(NowIncreasedPC), .sel(PCSel));
  Multiplexer #(.width(32)) multiplexer_2 (.in0(Instruction), .in1(32'h13), .out(NowInstruction), .sel(PCSel));
  Register #(.width(32)) PipePC (.D(ProgramCounter), .clk(clk), .Q(NextPC));  // open: en, clr
  Register #(.width(32)) PipeInst (.D(NowInstruction), .clk(clk), .Q({Immd, NextInstruction}));  // open: en, clr
  Register #(.width(32)) Pipe4PC (.D(NowIncreasedPC), .clk(clk), .Q(NextIncreasedPC));  // open: en, clr
  control_logic control_logic_1 (
    .Instruction({Immd, NextInstruction}), .BrEq(BrEq), .BrLt(BrLt), .PCSel(PCSel), .RegWEn(RegWEn),
    .ImmSel(ImmSel), .BrUn(BrUn), .ASel(ASel), .BSel(BSel), .ALUSel(ALUSel), .MemRW(MemRW), .WBSel(WBSel));
  imm_gen imm_gen_1 (.Instruction({Immd, NextInstruction}), .ImmSel(ImmSel), .Immediate(Immediate));
  branch_comp branch_comp_1 (.BrData1(ReadData1), .BrData2(ReadData2), .BrUn(BrUn), .BrEq(BrEq), .BrLt(BrLt));
  regfile regfile_1 (
    .ReadIndex1(NextInstruction[19:15]), .ReadIndex2(Immd[4:0]), .WriteIndex(NextInstruction[11:7]),
    .WriteData(WriteBack), .RegWEn(RegWEn), .clk(clk), .ra(ra), .sp(sp), .t0(t0), .t1(t1), .t2(t2), .s0(s0),
    .s1(s1), .a0(a0), .ReadData1(ReadData1), .ReadData2(ReadData2));
  Multiplexer #(.width(32)) multiplexer_3 (.in0(ReadData1), .in1(NextPC), .out(ALUInputA), .sel(ASel));
  Multiplexer #(.width(32)) multiplexer_4 (.in0(ReadData2), .in1(Immediate), .out(ALUInputB), .sel(BSel));
  alu alu_1 (.A(ALUInputA), .B(ALUInputB), .ALUSel(ALUSel), .ALUResult(MemAddress));
  partial_store partial_store_1 (
    .Instruction({Immd, NextInstruction}), .MemAddress(MemAddress), .DataFromReg(ReadData2), .MemRW(MemRW),
    .MemWriteMask(MemWriteMask), .DataToMem(MemWriteData));
  partial_load partial_load_1 (
    .Instruction({Immd, NextInstruction}), .MemAddress(MemAddress), .DataFromMem(MemReadData),
    .DataToReg(DataToReg));
  Multiplexer #(.select(2), .width(32)) multiplexer_5 (
    .in0(DataToReg), .in1(MemAddress), .in2(NextIncreasedPC), .out(WriteBack), .sel(WBSel));  // open: in3

  // Other names for the same wires on the sheet: ALUResult[31:0] = MemAddress; OP[6:0] = NextInstruction[6:0];
  //   rd1[4:0] = NextInstruction[11:7]; rs1[4:0] = NextInstruction[19:15]; NextInstruction[31:20] = Immd;
  //   rs2[4:0] = Immd[4:0]

  // Notes on the sheet:
  //   To IMEM
  //   IMEM (do **NOT** move this)
  //   From IMEM
  //   Inputs/Outputs for testing. Do **NOT** move these.
  //   To DMEM
  //   DMEM (do **NOT** move this)
  //   From DMEM
endmodule
