// Logisim project regfile.circ as structural Verilog: 1 circuit, main circuit regfile
module regfile (
  input  [4:0] ReadIndex1,
  input  [4:0] ReadIndex2,
  input  [4:0] WriteIndex,
  input  [31:0] WriteData,
  input  RegWEn,
  input  clk,
  output [31:0] ra,
  output [31:0] sp,
  output [31:0] t0,
  output [31:0] t1,
  output [31:0] t2,
  output [31:0] s0,
  output [31:0] s1,
  output [31:0] a0,
  output [31:0] ReadData1,
  output [31:0] ReadData2
);

  wire a0WE, decoder_1_out20, decoder_1_out29, raWE, s0WE, s1WE, spWE, t0WE, t1WE, t2WE, undriven,
       undriven_2, undriven_3, undriven_4, undriven_5, undriven_6, undriven_7, undriven_8, undriven_9,
       undriven_10, undriven_11, undriven_12, undriven_13, undriven_14, undriven_15, undriven_16,
       undriven_17, undriven_18, undriven_19, undriven_20, undriven_21, undriven_22, undriven_23,
       undriven_24, undriven_25, undriven_26, undriven_27, undriven_28, undriven_29, undriven_30,
       undriven_31, undriven_32, x3WE, x4WE, x11WE, x12WE, x13WE, x14WE, x15WE, x16WE, x17WE, x18WE, x19WE,
       x20WE, x21WE, x22WE, x23WE, x24WE, x25WE, x26WE, x27WE, x28WE, x29WE, x30WE, x31WE;
  wire [31:0] x0, x3, x4, x11, x12, x13, x14, x15, x16, x17, x18, x19, x20, x21, x22, x23, x24, x25, x26,
       x27, x28, x29, x30, x31;

  Multiplexer #(.select(5), .width(32)) multiplexer_1 (
    .in0(x0), .in1(ra), .in2(sp), .in3(x3), .in4(x4), .in5(t0), .in6(t1), .in7(t2), .in8(s0), .in9(s1),
    .in10(a0), .in11(x11), .in12(x12), .in13(x13), .in14(x14), .in15(x15), .in16(x16), .in17(x17),
    .in18(x18), .in19(x19), .in20(x20), .in21(x21), .in22(x22), .in23(x23), .in24(x24), .in25(x25),
    .in26(x26), .in27(x27), .in28(x28), .in29(x29), .in30(x30), .in31(x31), .out(ReadData1), .sel(ReadIndex1));
  Multiplexer #(.select(5), .width(32)) multiplexer_2 (
    .in0(x0), .in1(ra), .in2(sp), .in3(x3), .in4(x4), .in5(t0), .in6(t1), .in7(t2), .in8(s0), .in9(s1),
    .in10(a0), .in11(x11), .in12(x12), .in13(x13), .in14(x14), .in15(x15), .in16(x16), .in17(x17),
    .in18(x18), .in19(x19), .in20(x20), .in21(x21), .in22(x22), .in23(x23), .in24(x24), .in25(x25),
    .in26(x26), .in27(x27), .in28(x28), .in29(x29), .in30(x30), .in31(x31), .out(ReadData2), .sel(ReadIndex2));
  Decoder #(.select(5)) decoder_1 (
    .out1(raWE), .out2(spWE), .out3(x3WE), .out4(x4WE), .out5(t0WE), .out6(t1WE), .out7(t2WE), .out8(s0WE),
    .out9(s1WE), .out10(a0WE), .out11(x11WE), .out12(x12WE), .out13(x13WE), .out14(x14WE), .out15(x15WE),
    .out16(x16WE), .out17(x17WE), .out18(x18WE), .out19(x19WE), .out20(decoder_1_out20), .out21(x21WE),
    .out22(x22WE), .out23(x23WE), .out24(x24WE), .out25(x25WE), .out26(x26WE), .out27(x27WE), .out28(x28WE),
    .out29(decoder_1_out29), .out30(x30WE), .out31(x31WE), .sel(WriteIndex), .en(RegWEn));  // open: out0
  Register #(.width(32)) u_x0 (.D(WriteData), .en(1'b0), .clk(clk), .Q(x0), .clr(undriven));
  Register #(.width(32)) x7 (.D(WriteData), .en(t2WE), .clk(clk), .Q(t2), .clr(undriven_2));
  Register #(.width(32)) u_x14 (.D(WriteData), .en(x14WE), .clk(clk), .Q(x14), .clr(undriven_3));
  Register #(.width(32)) u_x21 (.D(WriteData), .en(x21WE), .clk(clk), .Q(x21), .clr(undriven_4));
  Register #(.width(32)) u_x28 (.D(WriteData), .en(x28WE), .clk(clk), .Q(x28), .clr(undriven_5));
  Register #(.width(32)) x1 (.D(WriteData), .en(raWE), .clk(clk), .Q(ra), .clr(undriven_6));
  Register #(.width(32)) x8 (.D(WriteData), .en(s0WE), .clk(clk), .Q(s0), .clr(undriven_7));
  Register #(.width(32)) u_x15 (.D(WriteData), .en(x15WE), .clk(clk), .Q(x15), .clr(undriven_8));
  Register #(.width(32)) u_x22 (.D(WriteData), .en(x22WE), .clk(clk), .Q(x22), .clr(undriven_9));
  Register #(.width(32)) u_x29 (.D(WriteData), .en(x29WE), .clk(clk), .Q(x29), .clr(undriven_10));
  Register #(.width(32)) x2 (.D(WriteData), .en(spWE), .clk(clk), .Q(sp), .clr(undriven_11));
  Register #(.width(32)) x9 (.D(WriteData), .en(s1WE), .clk(clk), .Q(s1), .clr(undriven_12));
  Register #(.width(32)) u_x16 (.D(WriteData), .en(x16WE), .clk(clk), .Q(x16), .clr(undriven_13));
  Register #(.width(32)) u_x23 (.D(WriteData), .en(x23WE), .clk(clk), .Q(x23), .clr(undriven_14));
  Register #(.width(32)) u_x30 (.D(WriteData), .en(x30WE), .clk(clk), .Q(x30), .clr(undriven_15));
  Register #(.width(32)) u_x3 (.D(WriteData), .en(x3WE), .clk(clk), .Q(x3), .clr(undriven_16));
  Register #(.width(32)) x10 (.D(WriteData), .en(a0WE), .clk(clk), .Q(a0), .clr(undriven_17));
  Register #(.width(32)) u_x17 (.D(WriteData), .en(x17WE), .clk(clk), .Q(x17), .clr(undriven_18));
  Register #(.width(32)) u_x24 (.D(WriteData), .en(x24WE), .clk(clk), .Q(x24), .clr(undriven_19));
  Register #(.width(32)) u_x31 (.D(WriteData), .en(x31WE), .clk(clk), .Q(x31), .clr(undriven_20));
  Register #(.width(32)) u_x4 (.D(WriteData), .en(x4WE), .clk(clk), .Q(x4), .clr(undriven_21));
  Register #(.width(32)) u_x11 (.D(WriteData), .en(x11WE), .clk(clk), .Q(x11), .clr(undriven_22));
  Register #(.width(32)) u_x18 (.D(WriteData), .en(x18WE), .clk(clk), .Q(x18), .clr(undriven_23));
  Register #(.width(32)) u_x25 (.D(WriteData), .en(x25WE), .clk(clk), .Q(x25), .clr(undriven_24));
  Register #(.width(32)) x5 (.D(WriteData), .en(t0WE), .clk(clk), .Q(t0), .clr(undriven_25));
  Register #(.width(32)) u_x12 (.D(WriteData), .en(x12WE), .clk(clk), .Q(x12), .clr(undriven_26));
  Register #(.width(32)) u_x19 (.D(WriteData), .en(x19WE), .clk(clk), .Q(x19), .clr(undriven_27));
  Register #(.width(32)) u_x26 (.D(WriteData), .en(x26WE), .clk(clk), .Q(x26), .clr(undriven_28));
  Register #(.width(32)) x6 (.D(WriteData), .en(t1WE), .clk(clk), .Q(t1), .clr(undriven_29));
  Register #(.width(32)) u_x13 (.D(WriteData), .en(x13WE), .clk(clk), .Q(x13), .clr(undriven_30));
  Register #(.width(32)) u_x20 (.D(WriteData), .en(x20WE), .clk(clk), .Q(x20), .clr(undriven_31));
  Register #(.width(32)) u_x27 (.D(WriteData), .en(x27WE), .clk(clk), .Q(x27), .clr(undriven_32));

  // Notes on the sheet:
  //   INPUTS to your circuit
  //   DON'T CHANGE THE LOCATIONS OF THE INPUTS AND OUTPUTS!
  //   These are DEBUG/TEST outputs from your circuit.
  //   OUTPUTS from your circuit
endmodule
