// Logisim project branch_complex.circ as structural Verilog: 1 circuit, main circuit run_main
module run_main (
  output [31:0] ra,
  output [31:0] sp,
  output [31:0] t0,
  output [31:0] t1,
  output [31:0] t2,
  output [31:0] s0,
  output [31:0] s1,
  output [31:0] a0,
  output [31:0] RequestedAddress,
  output [31:0] RequestedInstruction,
  output [15:0] TimeStep,
  output halt
);

  wire clk;

  Clock clock_1 (.out(clk));
  // Probe on RequestedAddress
  // cpu_harness cpu_harness_1: pin names not known; wires that end beside it: RequestedInstruction, clk, RequestedAddress, ra, sp, t0, t1, t2, s0, s1, a0
  ROM #(.addrWidth(14), .dataWidth(32)) rom_1 (.addr(RequestedAddress[15:2]), .data(RequestedInstruction));
  // Probe on RequestedInstruction
  Counter #(.max('hffff), .width(16)) counter_1 (.clk(clk), .Q(TimeStep));  // open: clr, load, up, count, D, carry
  Comparator #(.width(16)) comparator_1 (.a(TimeStep), .b(16'h9f), .eq(halt));  // open: gt, lt

  // Other names for the same wires on the sheet: Instruction[31:0] = RequestedInstruction;
  //   ProgramCounter[31:0] = RequestedAddress

  // Notes on the sheet:
  //   contents of rom_1 (hex, n*v repeats v):
  //   500293 500313 513 628463 463 100513 500293 600313 593 628663 100593 263 500293 500313 613 62d463 463
  //   100613 600293 500313 693 62d463 463 100693 500293 600313 713 62d663 100713 263 ffe00293 ffb00313 793
  //   62d463 463 100793 ffb00293 ffe00313 813 62d663 100813 263 500293 500313 893 62f463 463 100893 600293
  //   500313 913 62f463 463 100913 500293 600313 993 62f663 100993 263 fff00293 500313 a13 62f463 463
  //   100a13 500293 fff00313 a93 62f663 100a93 263 500293 600313 b13 62c463 463 100b13 600293 500313 b93
  //   62c663 100b93 263 500293 500313 c13 62c663 100c13 263 ffb00293 ffe00313 c93 62c463 463 100c93
  //   ffe00293 ffb00313 d13 62c663 100d13 263 500293 600313 d93 62e463 463 100d93 600293 500313 e13 62e663
  //   100e13 263 500293 500313 e93 62e663 100e93 263 500293 fff00313 f13 62e463 463 100f13 fff00293 500313
  //   f93 62e663 100f93 263 500293 600313 393 629463 463 100393 500293 500313 413 629663 100413 263
  //   Instruction Memory
  //   Halts Execution After Constant # of Clock Cycles
  //   Constant
endmodule
