// Logisim project test_arithmetic.circ as structural Verilog: 1 circuit, main circuit run_main
module run_main (
  output [31:0] ra,
  output [31:0] sp,
  output [31:0] t0,
  output [31:0] t1,
  output [31:0] t2,
  output [31:0] s0,
  output [31:0] s1,
  output [31:0] a0,
  output [31:0] RequestedAddress,
  output [31:0] RequestedInstruction,
  output [15:0] TimeStep,
  output halt
);

  wire clk;

  Clock clock_1 (.out(clk));
  // Probe on RequestedAddress
  // cpu_harness cpu_harness_1: pin names not known; wires that end beside it: RequestedInstruction, clk, RequestedAddress, ra, sp, t0, t1, t2, s0, s1, a0
  ROM #(.addrWidth(14), .dataWidth(32)) rom_1 (.addr(RequestedAddress[15:2]), .data(RequestedInstruction));
  // Probe on RequestedInstruction
  Counter #(.max('hffff), .width(16)) counter_1 (.clk(clk), .Q(TimeStep));  // open: clr, load, up, count, D, carry
  Comparator #(.width(16)) comparator_1 (.a(TimeStep), .b(16'h1d), .eq(halt));  // open: gt, lt

  // Other names for the same wires on the sheet: Instruction[31:0] = RequestedInstruction;
  //   ProgramCounter[31:0] = RequestedAddress

  // Notes on the sheet:
  //   contents of rom_1 (hex, n*v repeats v):
  //   a00293 1400313 6283b3 26283b3 406283b3 6293b3 26293b3 262b3b3 62a3b3 62c3b3 62d3b3 4062d3b3 62e3b3
  //   62f3b3 a28393 a29393 a2a393 a2c393 a2d393 40a2d393 a2e393 a2f393 ff628393 ff62a393 ff62c393 ff62e393
  //   ff62f393
  //   Instruction Memory
  //   Halts Execution After Constant # of Clock Cycles
  //   Constant
endmodule
