// Logisim project test_r-type_comprehensive.circ as structural Verilog: 1 circuit, main circuit run_main
module run_main (
  output [31:0] ra,
  output [31:0] sp,
  output [31:0] t0,
  output [31:0] t1,
  output [31:0] t2,
  output [31:0] s0,
  output [31:0] s1,
  output [31:0] a0,
  output [31:0] RequestedAddress,
  output [31:0] RequestedInstruction,
  output [15:0] TimeStep,
  output halt
);

  wire clk;

  Clock clock_1 (.out(clk));
  // Probe on RequestedAddress
  // cpu_harness cpu_harness_1: pin names not known; wires that end beside it: RequestedInstruction, clk, RequestedAddress, ra, sp, t0, t1, t2, s0, s1, a0
  ROM #(.addrWidth(14), .dataWidth(32)) rom_1 (.addr(RequestedAddress[15:2]), .data(RequestedInstruction));
  // Probe on RequestedInstruction
  Counter #(.max('hffff), .width(16)) counter_1 (.clk(clk), .Q(TimeStep));  // open: clr, load, up, count, D, carry
  Comparator #(.width(16)) comparator_1 (.a(TimeStep), .b(16'h53), .eq(halt));  // open: gt, lt

  // Other names for the same wires on the sheet: Instruction[31:0] = RequestedInstruction;
  //   ProgramCounter[31:0] = RequestedAddress

  // Notes on the sheet:
  //   contents of rom_1 (hex, n*v repeats v):
  //   a00293 1400313 6283b3 ffb00293 300313 6283b3 6400293 1e00313 406283b3 a00293 3200313 406283b3
  //   f000293 f00313 62f3b3 e000293 f000313 62f3b3 d000293 f00313 62e3b3 a000293 5500313 62e3b3 c100293
  //   c200313 62c3b3 12300293 12300313 62c3b3 100293 400313 6293b3 ff100293 100313 6293b3 ff000293 400313
  //   62d3b3 ff00293 800313 62d3b3 ff000293 400313 4062d3b3 40000293 200313 4062d3b3 a00293 1400313 62a3b3
  //   ff600293 fec00313 62a3b3 500293 500313 62a3b3 700293 800313 26283b3 ffe00293 7d000313 26283b3
  //   fff00293 fff00313 26283b3 3e800293 3e800313 26293b3 ffe00293 3e800313 26293b3 ff600293 fec00313
  //   26293b3 7d000293 7d000313 262b3b3 7ff00293 7ff00313 262b3b3
  //   Instruction Memory
  //   Halts Execution After Constant # of Clock Cycles
  //   Constant
endmodule
